# Fritzing sketch Setup (saved by Fritzing 0.9.3b)
circuit board: 8.46667cm x 5.64444cm
breadboards: 1

parts:
  Part1 = Arduino Uno (Rev3)
  Part2 = Arduino Uno (Rev3)
  Part3 = Bluetooth HC-05 Macho
  R1 = Resistor [tolerance=±5% resistance=220 package=THT]
  R2 = Resistor [tolerance=±5% resistance=220 package=THT]
  R3 = Resistor [tolerance=±5% resistance=220 package=THT]
  Part4 = Bluetooth HC-05 Macho
  R8 = Resistor [tolerance=±5% resistance=220 package=THT]
  R9 = Resistor [tolerance=±5% resistance=220 package=THT]
  R10 = Resistor [tolerance=±5% resistance=220 package=THT]
  LED6 = LED - 5mm [color="Red (633nm)" package="5 mm [THT]"]
  LED7 = LED - 5mm [color="Yellow (595nm)" package="5 mm [THT]"]
  LED8 = LED - 5mm [color="Green (565nm)" package="5 mm [THT]"]
  R11 = Resistor [tolerance=±5% resistance=220 package=THT]
  R12 = Resistor [tolerance=±5% resistance=220 package=THT]
  R13 = Resistor [tolerance=±5% resistance=220 package=THT]
  LED5 = LED - 5mm [color="Red (633nm)" package="5 mm [THT]"]
  R14 = Trimmer Potentiometer [maximum_resistance=10kΩ package=THT]
  LED9 = LED - 5mm [color="Red (633nm)" package="5 mm [THT]"]

nets:
  N1: Part1.A0, R14.wiper
  N2: Part1.D12/MISO, R9.Pin_1
  N3: Part1.D13/SCK, Part4.TXD
  GND: Part1.GND, Part4.GND, R10.Pin_0, LED5.cathode, R14.leg2
  5V: Part1.5V, Part4.VCC, R14.leg1
  N4: Part2.D8, LED7.cathode
  N5: Part2.D9_PWM, LED6.cathode
  N6: Part2.D12/MISO, R1.Pin_0
  N7: Part2.D13/SCK, Part3.TXD
  N8: Part2.D7, LED8.cathode
  5V_2: Part2.5V, Part3.VCC
  GND_2: Part2.GND, Part3.GND, R3.Pin_0, R11.Pin_1, R12.Pin_1, R13.Pin_1, LED9.cathode
  N9: Part3.State, LED9.anode
  N10: Part3.RXD, R2.Pin_1, R3.Pin_1
  N11: R1.Pin_1, R2.Pin_0
  N12: Part4.State, LED5.anode
  N13: Part4.RXD, R8.Pin_1, R9.Pin_0
  N14: R8.Pin_0, R10.Pin_1
  N15: LED6.anode, R11.Pin_0
  N16: LED7.anode, R12.Pin_0
  N17: LED8.anode, R13.Pin_0
